// Logisim project HuuCao_DigitalClock.circ as structural Verilog: 7 circuits, main circuit Clock-Control
module Clock_Control (
  input  in_1,
  input  Clock,
  input  in_3,
  input  in_4,
  output a,
  output b,
  output c,
  output d,
  output e,
  output f,
  output g,
  output a_2,
  output b_2,
  output c_2,
  output d_2,
  output e_2,
  output f_2,
  output g_2,
  output out_19,
  output a_3,
  output b_3,
  output c_3,
  output d_3,
  output e_3,
  output f_3,
  output g_3,
  output a_4,
  output b_4,
  output c_4,
  output d_4,
  output e_4,
  output f_4,
  output g_4,
  output a_5,
  output b_5,
  output c_5,
  output d_5,
  output g_5,
  output e_5,
  output f_5,
  output g_6,
  output Separator,
  output a_6,
  output b_6,
  output c_6,
  output d_6,
  output e_6,
  output f_6
);

  wire counter_2_1_x0, counter_2_1_x1, counter_2_1_x2, counter_2_1_x3, counter_6_1_x0, counter_6_1_x1,
       counter_6_1_x2, counter_6_1_x3, counter_6_2_x0, counter_6_2_x1, counter_6_2_x2, counter_6_2_x3,
       counter_10_1_x0, counter_10_1_x1, counter_10_1_x2, counter_10_1_x3, counter_10_2_x0, counter_10_2_x1,
       counter_10_2_x2, counter_10_2_x3, counter_23_1_x0, counter_23_1_x1, counter_23_1_x2, counter_23_1_x3,
       counter_23_1_x4, n5_bit_7_segment_control_1_carryout, n5_bit_7_segment_control_2_carryout,
       n5_bit_7_segment_control_3_carryout, n5_bit_7_segment_control_4_carryout,
       n5_bit_7_segment_control_5_carryout, or_1_out, or_2_out, or_3_out;

  or or_1 (or_1_out, in_1, Clock);
  or or_2 (or_2_out, in_3, n5_bit_7_segment_control_2_carryout);
  or or_3 (or_3_out, in_4, n5_bit_7_segment_control_4_carryout);
  Counter_10 counter_10_1 (
    .Clock(or_1_out), .x3(counter_10_1_x3), .x2(counter_10_1_x2), .x1(counter_10_1_x1), .x0(counter_10_1_x0));
  Counter_6 counter_6_1 (
    .Clock(n5_bit_7_segment_control_1_carryout), .x3(counter_6_1_x3), .x2(counter_6_1_x2),
    .x1(counter_6_1_x1), .x0(counter_6_1_x0));
  Counter_10 counter_10_2 (
    .Clock(or_2_out), .x3(counter_10_2_x3), .x2(counter_10_2_x2), .x1(counter_10_2_x1), .x0(counter_10_2_x0));
  Counter_6 counter_6_2 (
    .Clock(n5_bit_7_segment_control_3_carryout), .x3(counter_6_2_x3), .x2(counter_6_2_x2),
    .x1(counter_6_2_x1), .x0(counter_6_2_x0));
  Counter_23 counter_23_1 (
    .Clock(or_3_out), .x4(counter_23_1_x4), .x3(counter_23_1_x3), .x2(counter_23_1_x2), .x1(counter_23_1_x1),
    .x0(counter_23_1_x0));
  Counter_2 counter_2_1 (
    .Clock(n5_bit_7_segment_control_5_carryout), .x3(counter_2_1_x3), .x2(counter_2_1_x2),
    .x1(counter_2_1_x1), .x0(counter_2_1_x0));
  _5_bit_7_Segment_Control u_5_bit_7_segment_control_1 (
    .x4(1'b0), .x3(counter_10_1_x3), .x2(counter_10_1_x2), .x1(counter_10_1_x1), .x0(counter_10_1_x0), .a(a),
    .b(b), .c(c), .d(d), .e(e), .f(f), .g(g), .CarryOut(n5_bit_7_segment_control_1_carryout));
  _5_bit_7_Segment_Control u_5_bit_7_segment_control_2 (
    .x4(1'b0), .x3(counter_6_1_x3), .x2(counter_6_1_x2), .x1(counter_6_1_x1), .x0(counter_6_1_x0), .a(a_2),
    .b(b_2), .c(c_2), .d(d_2), .e(e_2), .f(f_2), .g(g_2), .CarryOut(n5_bit_7_segment_control_2_carryout));
  _5_bit_7_Segment_Control u_5_bit_7_segment_control_3 (
    .x4(1'b0), .x3(counter_10_2_x3), .x2(counter_10_2_x2), .x1(counter_10_2_x1), .x0(counter_10_2_x0),
    .a(a_3), .b(b_3), .c(c_3), .d(d_3), .e(e_3), .f(f_3), .g(g_3),
    .CarryOut(n5_bit_7_segment_control_3_carryout));
  _5_bit_7_Segment_Control u_5_bit_7_segment_control_4 (
    .x4(1'b0), .x3(counter_6_2_x3), .x2(counter_6_2_x2), .x1(counter_6_2_x1), .x0(counter_6_2_x0), .a(a_4),
    .b(b_4), .c(c_4), .d(d_4), .e(e_4), .f(f_4), .g(g_4), .CarryOut(n5_bit_7_segment_control_4_carryout));
  _5_bit_7_Segment_Control u_5_bit_7_segment_control_5 (
    .x4(counter_23_1_x4), .x3(counter_23_1_x3), .x2(counter_23_1_x2), .x1(counter_23_1_x1),
    .x0(counter_23_1_x0), .a(a_5), .b(b_5), .c(c_5), .d(d_5), .e(e_5), .f(f_5), .g(g_6),
    .CarryOut(n5_bit_7_segment_control_5_carryout));
  _5_bit_7_Segment_Control u_5_bit_7_segment_control_6 (
    .x4(1'b0), .x3(counter_2_1_x3), .x2(counter_2_1_x2), .x1(counter_2_1_x1), .x0(counter_2_1_x0), .a(a_6),
    .b(b_6), .c(c_6), .d(d_6), .e(e_6), .f(f_6), .g(g_5));  // open: CarryOut

  assign out_19 = 1'b1;
  assign Separator = 1'b1;
endmodule

module Counter_10 (
  input  Clock,
  output x3,
  output x2,
  output x1,
  output x0
);

  wire and_1_out, and_2_out, and_3_out, and_4_out, and_5_out, and_6_out, and_7_out, and_8_out, and_9_out,
       not_1_out, not_2_out, not_3_out, not_4_out, not_5_out, not_6_out, not_7_out, not_8_out, not_9_out,
       not_10_out, not_11_out, not_12_out, not_13_out, not_14_out, not_15_out, not_16_out, not_17_out,
       not_18_out, not_19_out, or_1_out, or_2_out, or_3_out, or_4_out;

  not not_1 (not_1_out, x3);
  not not_2 (not_2_out, x2);
  not not_3 (not_3_out, x1);
  not not_4 (not_4_out, x0);
  not not_5 (not_5_out, x3);
  not not_6 (not_6_out, x2);
  not not_7 (not_7_out, x3);
  not not_8 (not_8_out, x1);
  not not_9 (not_9_out, x3);
  not not_10 (not_10_out, x0);
  not not_11 (not_11_out, x3);
  not not_12 (not_12_out, x1);
  not not_13 (not_13_out, x3);
  not not_14 (not_14_out, x0);
  not not_15 (not_15_out, x3);
  not not_16 (not_16_out, x0);
  not not_17 (not_17_out, x2);
  not not_18 (not_18_out, x1);
  not not_19 (not_19_out, x0);
  and and_1 (and_1_out, not_1_out, x2, x1, x0);
  and and_2 (and_2_out, x3, not_2_out, not_3_out, not_4_out);
  and and_3 (and_3_out, not_5_out, not_6_out, x1, x0);
  and and_4 (and_4_out, not_7_out, x2, not_8_out);
  and and_5 (and_5_out, not_9_out, x2, not_10_out);
  and and_6 (and_6_out, not_11_out, not_12_out, x0);
  and and_7 (and_7_out, not_13_out, x1, not_14_out);
  and and_8 (and_8_out, not_15_out, not_16_out);
  and and_9 (and_9_out, not_17_out, not_18_out, not_19_out);
  or or_1 (or_1_out, and_1_out, and_2_out);
  or or_2 (or_2_out, and_3_out, and_4_out, and_5_out);
  or or_3 (or_3_out, and_6_out, and_7_out);
  or or_4 (or_4_out, and_8_out, and_9_out);
  D_Flip_Flop d_ff_1 (.clk(Clock), .D(or_1_out), .Q(x3));  // open: Qn, preset, en, reset
  D_Flip_Flop d_ff_2 (.clk(Clock), .D(or_2_out), .Q(x2));  // open: Qn, preset, en, reset
  D_Flip_Flop d_ff_3 (.clk(Clock), .D(or_3_out), .Q(x1));  // open: Qn, preset, en, reset
  D_Flip_Flop d_ff_4 (.clk(Clock), .D(or_4_out), .Q(x0));  // open: Qn, preset, en, reset
endmodule

module Counter_6 (
  input  Clock,
  output x3,
  output x2,
  output x1,
  output x0
);

  wire and_1_out, and_2_out, and_3_out, and_4_out, and_5_out, and_6_out, not_1_out, not_2_out, not_3_out,
       not_4_out, not_5_out, not_6_out, not_7_out, not_8_out, not_9_out, not_10_out, not_11_out, not_12_out,
       not_13_out, not_14_out, not_15_out, not_16_out, not_17_out, or_1_out, or_2_out, or_3_out;

  not not_1 (not_1_out, x3);
  not not_2 (not_2_out, x2);
  not not_3 (not_3_out, x3);
  not not_4 (not_4_out, x1);
  not not_5 (not_5_out, x0);
  not not_6 (not_6_out, x3);
  not not_7 (not_7_out, x2);
  not not_8 (not_8_out, x1);
  not not_9 (not_9_out, x3);
  not not_10 (not_10_out, x2);
  not not_11 (not_11_out, x0);
  not not_12 (not_12_out, x3);
  not not_13 (not_13_out, x2);
  and and_1 (and_1_out, not_12_out, not_13_out, not_14_out);
  not not_14 (not_14_out, x0);
  not not_15 (not_15_out, x3);
  and and_2 (and_2_out, not_15_out, not_16_out, not_17_out);
  not not_16 (not_16_out, x1);
  not not_17 (not_17_out, x0);
  and and_3 (and_3_out, not_1_out, not_2_out, x1, x0);
  or or_1 (or_1_out, and_3_out, and_4_out);
  and and_4 (and_4_out, not_3_out, x2, not_4_out, not_5_out);
  and and_5 (and_5_out, not_6_out, not_7_out, not_8_out, x0);
  or or_2 (or_2_out, and_5_out, and_6_out);
  and and_6 (and_6_out, not_9_out, not_10_out, x1, not_11_out);
  or or_3 (or_3_out, and_1_out, and_2_out);
  D_Flip_Flop d_ff_1 (.clk(Clock), .D(1'b0), .Q(x3));  // open: Qn, preset, en, reset
  D_Flip_Flop d_ff_2 (.clk(Clock), .D(or_1_out), .Q(x2));  // open: Qn, preset, en, reset
  D_Flip_Flop d_ff_3 (.clk(Clock), .D(or_2_out), .Q(x1));  // open: Qn, preset, en, reset
  D_Flip_Flop d_ff_4 (.clk(Clock), .D(or_3_out), .Q(x0));  // open: Qn, preset, en, reset
endmodule

module Counter_2 (
  input  Clock,
  output x3,
  output x2,
  output x1,
  output x0
);

  wire and_1_out, and_2_out, not_1_out, not_2_out, not_3_out, not_4_out, not_5_out, not_6_out, not_7_out;

  not not_1 (not_1_out, x3);
  not not_2 (not_2_out, x2);
  not not_3 (not_3_out, x1);
  not not_4 (not_4_out, x3);
  not not_5 (not_5_out, x2);
  not not_6 (not_6_out, x1);
  not not_7 (not_7_out, x0);
  and and_1 (and_1_out, not_1_out, not_2_out, not_3_out, x0);
  and and_2 (and_2_out, not_4_out, not_5_out, not_6_out, not_7_out);
  D_Flip_Flop d_ff_1 (.clk(Clock), .D(1'b0), .Q(x3));  // open: Qn, preset, en, reset
  D_Flip_Flop d_ff_2 (.clk(Clock), .D(1'b0), .Q(x2));  // open: Qn, preset, en, reset
  D_Flip_Flop d_ff_3 (.clk(Clock), .D(and_1_out), .Q(x1));  // open: Qn, preset, en, reset
  D_Flip_Flop d_ff_4 (.clk(Clock), .D(and_2_out), .Q(x0));  // open: Qn, preset, en, reset
endmodule

module _5_bit_7_Segment_Control (
  input  x4,
  input  x3,
  input  x2,
  input  x1,
  input  x0,
  output a,
  output b,
  output c,
  output d,
  output e,
  output f,
  output g,
  output CarryOut
);

  wire and_1_out, and_2_out, and_3_out, and_4_out, and_5_out, and_6_out, and_7_out, and_8_out, and_9_out,
       and_10_out, and_11_out, and_12_out, and_13_out, and_14_out, and_15_out, and_16_out, and_17_out,
       and_18_out, and_19_out, and_20_out, and_21_out, and_22_out, and_23_out, and_24_out, and_25_out,
       and_26_out, and_27_out, and_28_out, and_29_out, and_30_out, and_31_out, and_32_out, and_33_out,
       and_34_out, and_35_out, and_36_out, and_37_out, and_38_out, and_39_out, and_40_out, and_41_out,
       and_42_out, and_43_out, and_44_out, and_45_out, and_46_out, and_47_out, and_48_out, and_49_out,
       and_50_out, and_51_out, and_52_out, and_53_out, and_54_out, and_55_out, and_56_out, and_57_out,
       and_58_out, and_59_out, and_60_out, not_1_out, not_2_out, not_3_out, not_4_out, not_5_out, not_6_out,
       not_7_out, not_8_out, not_9_out, not_10_out, not_11_out, not_12_out, not_13_out, not_14_out,
       not_15_out, not_16_out, not_17_out, not_18_out, not_19_out, not_20_out, not_21_out, not_22_out,
       not_23_out, not_24_out, not_25_out, not_26_out, not_27_out, not_28_out, not_29_out, not_30_out,
       not_31_out, not_32_out, not_33_out, not_34_out, not_35_out, not_36_out, not_37_out, not_38_out,
       not_39_out, not_40_out, not_41_out, not_42_out, not_43_out, not_44_out, not_45_out, not_46_out,
       not_47_out, not_48_out, not_49_out, not_50_out, not_51_out, not_52_out, not_53_out, not_54_out,
       not_55_out, not_56_out, not_57_out, not_58_out, not_59_out, not_60_out, not_61_out, not_62_out,
       not_63_out, not_64_out, not_65_out, not_66_out, not_67_out, not_68_out, not_69_out, not_70_out,
       not_71_out, not_72_out, not_73_out, not_74_out, not_75_out, not_76_out, not_77_out, not_78_out,
       not_79_out, not_80_out, not_81_out, not_82_out, not_83_out, not_84_out, not_85_out, not_86_out,
       not_87_out, not_88_out, not_89_out, not_90_out, not_91_out, not_92_out, not_93_out, not_94_out,
       not_95_out, not_96_out, not_97_out, not_98_out, not_99_out, not_100_out, not_101_out, not_102_out,
       not_103_out, not_104_out, not_105_out, not_106_out, not_107_out, not_108_out, not_109_out;

  not not_1 (not_1_out, x4);
  not not_2 (not_2_out, x2);
  not not_3 (not_3_out, x0);
  not not_4 (not_4_out, x3);
  not not_5 (not_5_out, x4);
  not not_6 (not_6_out, x4);
  not not_7 (not_7_out, x1);
  not not_8 (not_8_out, x1);
  not not_9 (not_9_out, x3);
  not not_10 (not_10_out, x0);
  not not_11 (not_11_out, x2);
  not not_12 (not_12_out, x0);
  not not_13 (not_13_out, x4);
  not not_14 (not_14_out, x2);
  not not_15 (not_15_out, x4);
  not not_16 (not_16_out, x1);
  not not_17 (not_17_out, x0);
  not not_18 (not_18_out, x3);
  not not_19 (not_19_out, x2);
  not not_20 (not_20_out, x3);
  not not_21 (not_21_out, x2);
  not not_22 (not_22_out, x3);
  not not_23 (not_23_out, x2);
  not not_24 (not_24_out, x4);
  not not_25 (not_25_out, x0);
  not not_26 (not_26_out, x1);
  not not_27 (not_27_out, x0);
  not not_28 (not_28_out, x1);
  not not_29 (not_29_out, x3);
  not not_30 (not_30_out, x1);
  not not_31 (not_31_out, x4);
  not not_32 (not_32_out, x3);
  not not_33 (not_33_out, x2);
  not not_34 (not_34_out, x2);
  not not_35 (not_35_out, x1);
  not not_36 (not_36_out, x4);
  not not_37 (not_37_out, x2);
  not not_38 (not_38_out, x0);
  not not_39 (not_39_out, x3);
  not not_40 (not_40_out, x2);
  not not_41 (not_41_out, x0);
  not not_42 (not_42_out, x3);
  not not_43 (not_43_out, x2);
  not not_44 (not_44_out, x3);
  not not_45 (not_45_out, x0);
  not not_46 (not_46_out, x2);
  not not_47 (not_47_out, x0);
  not not_48 (not_48_out, x4);
  not not_49 (not_49_out, x1);
  not not_50 (not_50_out, x1);
  not not_51 (not_51_out, x1);
  not not_52 (not_52_out, x4);
  not not_53 (not_53_out, x3);
  not not_54 (not_54_out, x0);
  not not_55 (not_55_out, x4);
  not not_56 (not_56_out, x2);
  not not_57 (not_57_out, x0);
  not not_58 (not_58_out, x3);
  not not_59 (not_59_out, x2);
  not not_60 (not_60_out, x0);
  not not_61 (not_61_out, x3);
  not not_62 (not_62_out, x0);
  not not_63 (not_63_out, x2);
  not not_64 (not_64_out, x0);
  not not_65 (not_65_out, x4);
  not not_66 (not_66_out, x1);
  not not_67 (not_67_out, x0);
  not not_68 (not_68_out, x0);
  not not_69 (not_69_out, x3);
  not not_70 (not_70_out, x1);
  not not_71 (not_71_out, x0);
  not not_72 (not_72_out, x4);
  not not_73 (not_73_out, x3);
  not not_74 (not_74_out, x1);
  not not_75 (not_75_out, x4);
  not not_76 (not_76_out, x3);
  not not_77 (not_77_out, x0);
  not not_78 (not_78_out, x2);
  not not_79 (not_79_out, x1);
  not not_80 (not_80_out, x0);
  not not_81 (not_81_out, x4);
  not not_82 (not_82_out, x3);
  not not_83 (not_83_out, x2);
  not not_84 (not_84_out, x1);
  not not_85 (not_85_out, x3);
  not not_86 (not_86_out, x2);
  not not_87 (not_87_out, x3);
  not not_88 (not_88_out, x0);
  not not_89 (not_89_out, x4);
  not not_90 (not_90_out, x1);
  not not_91 (not_91_out, x1);
  not not_92 (not_92_out, x4);
  not not_93 (not_93_out, x2);
  not not_94 (not_94_out, x0);
  not not_95 (not_95_out, x3);
  not not_96 (not_96_out, x4);
  not not_97 (not_97_out, x2);
  not not_98 (not_98_out, x0);
  not not_99 (not_99_out, x3);
  not not_100 (not_100_out, x1);
  not not_101 (not_101_out, x0);
  not not_102 (not_102_out, x2);
  not not_103 (not_103_out, x1);
  not not_104 (not_104_out, x0);
  not not_105 (not_105_out, x4);
  not not_106 (not_106_out, x3);
  not not_107 (not_107_out, x2);
  not not_108 (not_108_out, x1);
  not not_109 (not_109_out, x0);
  and and_1 (and_1_out, not_1_out, not_2_out, not_3_out);
  and and_2 (and_2_out, not_4_out, x1);
  and and_3 (and_3_out, not_5_out, x2, x0);
  and and_4 (and_4_out, not_6_out, x3, not_7_out);
  and and_5 (and_5_out, x3, x2, not_8_out);
  and and_6 (and_6_out, x4, not_9_out, not_10_out);
  and and_7 (and_7_out, x4, not_11_out, x0);
  and and_8 (and_8_out, x4, x1, not_12_out);
  and and_9 (and_9_out, not_13_out, not_14_out);
  and and_10 (and_10_out, not_15_out, not_16_out, not_17_out);
  and and_11 (and_11_out, not_18_out, not_19_out, x0);
  and and_12 (and_12_out, not_20_out, not_21_out, x1);
  and and_13 (and_13_out, not_22_out, x1, x0);
  and and_14 (and_14_out, not_23_out, x1, x0);
  and and_15 (and_15_out, not_24_out, x3, not_25_out);
  and and_16 (and_16_out, x3, not_26_out, not_27_out);
  and and_17 (and_17_out, x3, x2, not_28_out);
  and and_18 (and_18_out, x4, x2);
  and and_19 (and_19_out, not_29_out, not_30_out);
  and and_20 (and_20_out, not_31_out, not_32_out, x2);
  and and_21 (and_21_out, x3, not_33_out);
  and and_22 (and_22_out, x3, x1);
  and and_23 (and_23_out, x4, not_34_out);
  and and_24 (and_24_out, x4, not_35_out);
  and and_25 (and_25_out, not_36_out, not_37_out, not_38_out);
  and and_26 (and_26_out, not_39_out, not_40_out, not_41_out);
  and and_27 (and_27_out, not_42_out, not_43_out, x1);
  and and_28 (and_28_out, not_44_out, x1, not_45_out);
  and and_29 (and_29_out, not_46_out, x1, not_47_out);
  and and_30 (and_30_out, not_48_out, x2, not_49_out, x0);
  and and_31 (and_31_out, x3, not_50_out, x0);
  and and_32 (and_32_out, x3, x2, not_51_out);
  and and_33 (and_33_out, not_52_out, x3, x2, x0);
  and and_34 (and_34_out, x4, not_53_out, x1);
  and and_35 (and_35_out, x4, x2, not_54_out);
  and and_36 (and_36_out, not_55_out, not_56_out, not_57_out);
  and and_37 (and_37_out, not_58_out, not_59_out, not_60_out);
  and and_38 (and_38_out, not_61_out, x1, not_62_out);
  and and_39 (and_39_out, not_63_out, x1, not_64_out);
  and and_40 (and_40_out, not_65_out, x3, not_66_out, not_67_out);
  and and_41 (and_41_out, x4, x2, not_68_out);
  and and_42 (and_42_out, not_69_out, not_70_out, not_71_out);
  and and_43 (and_43_out, not_72_out, not_73_out, x2, not_74_out);
  and and_44 (and_44_out, not_75_out, not_76_out, x2, not_77_out);
  and and_45 (and_45_out, x3, not_78_out, not_79_out);
  and and_46 (and_46_out, x3, x1, not_80_out);
  and and_47 (and_47_out, not_81_out, x3, x2, x1);
  and and_48 (and_48_out, x4, not_82_out, not_83_out, x1);
  and and_49 (and_49_out, x4, x3, not_84_out);
  and and_50 (and_50_out, not_85_out, not_86_out, x1);
  and and_51 (and_51_out, not_87_out, x1, not_88_out);
  and and_52 (and_52_out, not_89_out, x2, not_90_out);
  and and_53 (and_53_out, x3, not_91_out);
  and and_54 (and_54_out, not_92_out, x3, x2);
  and and_55 (and_55_out, x4, not_93_out, not_94_out);
  and and_56 (and_56_out, x4, not_95_out, x1);
  and and_57 (and_57_out, not_96_out, x3, not_97_out, x1, not_98_out);
  and and_58 (and_58_out, x4, not_99_out, x2, not_100_out, not_101_out);
  and and_59 (and_59_out, x4, x3, not_102_out, not_103_out, not_104_out);
  and and_60 (and_60_out, not_105_out, not_106_out, not_107_out, not_108_out, not_109_out);
  or or_1 (a, and_1_out, and_2_out, and_3_out, and_4_out, and_5_out, and_6_out, and_7_out, and_8_out);
  or or_2 (b, and_9_out, and_10_out, and_11_out, and_12_out, and_13_out, and_14_out, and_15_out, and_16_out, and_17_out, and_18_out);
  or or_3 (c, and_19_out, x0, and_20_out, and_21_out, and_22_out, and_23_out, and_24_out);
  or or_4 (d, and_25_out, and_26_out, and_27_out, and_28_out, and_29_out, and_30_out, and_31_out, and_32_out, and_33_out, and_34_out, and_35_out);
  or or_5 (e, and_36_out, and_37_out, and_38_out, and_39_out, and_40_out, and_41_out);
  or or_6 (f, and_42_out, and_43_out, and_44_out, and_45_out, and_46_out, and_47_out, and_48_out, and_49_out);
  or or_7 (g, and_50_out, and_51_out, and_52_out, and_53_out, and_54_out, and_55_out, and_56_out);
  or or_8 (CarryOut, and_57_out, and_58_out, and_59_out, and_60_out);
endmodule

module Counter_23 (
  input  Clock,
  output x4,
  output x3,
  output x2,
  output x1,
  output x0
);

  wire and_1_out, and_2_out, and_3_out, and_4_out, and_5_out, and_6_out, and_7_out, and_8_out, and_9_out,
       and_10_out, and_11_out, and_12_out, and_13_out, and_14_out, and_15_out, and_16_out, and_17_out,
       and_18_out, and_19_out, and_20_out, not_1_out, not_2_out, not_3_out, not_4_out, not_5_out, not_6_out,
       not_7_out, not_8_out, not_9_out, not_10_out, not_11_out, not_12_out, not_13_out, not_14_out,
       not_15_out, not_16_out, not_17_out, not_18_out, not_19_out, not_20_out, not_21_out, not_22_out,
       not_23_out, not_24_out, not_25_out, not_26_out, not_27_out, not_28_out, not_29_out, not_30_out,
       not_31_out, not_32_out, not_33_out, not_34_out, not_35_out, not_36_out, not_37_out, not_38_out,
       not_39_out, or_1_out, or_2_out, or_3_out, or_4_out, or_5_out;

  not not_1 (not_1_out, x4);
  not not_2 (not_2_out, x3);
  not not_3 (not_3_out, x2);
  not not_4 (not_4_out, x3);
  not not_5 (not_5_out, x1);
  not not_6 (not_6_out, x3);
  not not_7 (not_7_out, x0);
  not not_8 (not_8_out, x4);
  not not_9 (not_9_out, x3);
  not not_10 (not_10_out, x4);
  not not_11 (not_11_out, x2);
  not not_12 (not_12_out, x4);
  not not_13 (not_13_out, x1);
  not not_14 (not_14_out, x4);
  not not_15 (not_15_out, x0);
  not not_16 (not_16_out, x4);
  not not_17 (not_17_out, x2);
  not not_18 (not_18_out, x3);
  not not_19 (not_19_out, x2);
  not not_20 (not_20_out, x4);
  not not_21 (not_21_out, x1);
  not not_22 (not_22_out, x4);
  not not_23 (not_23_out, x0);
  not not_24 (not_24_out, x3);
  not not_25 (not_25_out, x1);
  not not_26 (not_26_out, x3);
  not not_27 (not_27_out, x0);
  not not_28 (not_28_out, x4);
  not not_29 (not_29_out, x1);
  not not_30 (not_30_out, x3);
  not not_31 (not_31_out, x1);
  not not_32 (not_32_out, x4);
  not not_33 (not_33_out, x0);
  not not_34 (not_34_out, x3);
  not not_35 (not_35_out, x0);
  not not_36 (not_36_out, x4);
  not not_37 (not_37_out, x0);
  not not_38 (not_38_out, x3);
  not not_39 (not_39_out, x0);
  and and_1 (and_1_out, not_1_out, x3, x2, x1, x0);
  and and_2 (and_2_out, x4, not_2_out, not_3_out);
  and and_3 (and_3_out, x4, not_4_out, not_5_out);
  and and_4 (and_4_out, x4, not_6_out, not_7_out);
  and and_5 (and_5_out, not_8_out, not_9_out, x2, x1, x0);
  and and_6 (and_6_out, not_10_out, x3, not_11_out);
  and and_7 (and_7_out, not_12_out, x3, not_13_out);
  and and_8 (and_8_out, not_14_out, x3, not_15_out);
  and and_9 (and_9_out, not_16_out, not_17_out, x1, x0);
  and and_10 (and_10_out, not_18_out, not_19_out, x1, x0);
  and and_11 (and_11_out, not_20_out, x2, not_21_out);
  and and_12 (and_12_out, not_22_out, x2, not_23_out);
  and and_13 (and_13_out, not_24_out, x2, not_25_out);
  and and_14 (and_14_out, not_26_out, x2, not_27_out);
  and and_15 (and_15_out, not_28_out, not_29_out, x0);
  and and_16 (and_16_out, not_30_out, not_31_out, x0);
  and and_17 (and_17_out, not_32_out, x1, not_33_out);
  and and_18 (and_18_out, not_34_out, x1, not_35_out);
  and and_19 (and_19_out, not_36_out, not_37_out);
  and and_20 (and_20_out, not_38_out, not_39_out);
  or or_1 (or_1_out, and_1_out, and_2_out, and_3_out, and_4_out);
  or or_2 (or_2_out, and_5_out, and_6_out, and_7_out, and_8_out);
  or or_3 (or_3_out, and_9_out, and_10_out, and_11_out, and_12_out, and_13_out, and_14_out);
  or or_4 (or_4_out, and_15_out, and_16_out, and_17_out, and_18_out);
  or or_5 (or_5_out, and_19_out, and_20_out);
  D_Flip_Flop d_ff_1 (.clk(Clock), .D(or_1_out), .Q(x4));  // open: Qn, preset, en, reset
  D_Flip_Flop d_ff_2 (.clk(Clock), .D(or_2_out), .Q(x3));  // open: Qn, preset, en, reset
  D_Flip_Flop d_ff_3 (.clk(Clock), .D(or_3_out), .Q(x2));  // open: Qn, preset, en, reset
  D_Flip_Flop d_ff_4 (.clk(Clock), .D(or_4_out), .Q(x1));  // open: Qn, preset, en, reset
  D_Flip_Flop d_ff_5 (.clk(Clock), .D(or_5_out), .Q(x0));  // open: Qn, preset, en, reset
endmodule

module Clock (
);

  wire clock_1_out, clock_control_1_a, clock_control_1_a_2, clock_control_1_a_3, clock_control_1_a_4,
       clock_control_1_a_5, clock_control_1_a_6, clock_control_1_b, clock_control_1_b_2, clock_control_1_b_3,
       clock_control_1_b_4, clock_control_1_b_5, clock_control_1_b_6, clock_control_1_c, clock_control_1_c_2,
       clock_control_1_c_3, clock_control_1_c_4, clock_control_1_c_5, clock_control_1_c_6, clock_control_1_d,
       clock_control_1_d_2, clock_control_1_d_3, clock_control_1_d_4, clock_control_1_d_5,
       clock_control_1_d_6, clock_control_1_e, clock_control_1_e_2, clock_control_1_e_3, clock_control_1_e_4,
       clock_control_1_e_5, clock_control_1_e_6, clock_control_1_f, clock_control_1_f_2, clock_control_1_f_3,
       clock_control_1_f_4, clock_control_1_f_5, clock_control_1_f_6, clock_control_1_g, clock_control_1_g_2,
       clock_control_1_g_3, clock_control_1_g_4, clock_control_1_g_5, clock_control_1_g_6,
       clock_control_1_out_19, clock_control_1_separator, Hour_up_out, Minute_up_out, Second_up_out;

  Clock_Control clock_control_1 (
    .a_3(clock_control_1_a_3), .b_3(clock_control_1_b_3), .c_3(clock_control_1_c_3),
    .d_3(clock_control_1_d_3), .e_3(clock_control_1_e_3), .f_3(clock_control_1_f_3),
    .g_3(clock_control_1_g_3), .a_4(clock_control_1_a_4), .b_4(clock_control_1_b_4),
    .c_4(clock_control_1_c_4), .d_4(clock_control_1_d_4), .e_4(clock_control_1_e_4),
    .f_4(clock_control_1_f_4), .g_4(clock_control_1_g_4), .a_5(clock_control_1_a_5),
    .b_5(clock_control_1_b_5), .c_5(clock_control_1_c_5), .d_5(clock_control_1_d_5),
    .e_5(clock_control_1_e_5), .f_5(clock_control_1_f_5), .g_6(clock_control_1_g_6),
    .a_6(clock_control_1_a_6), .b_6(clock_control_1_b_6), .c_6(clock_control_1_c_6),
    .d_6(clock_control_1_d_6), .e_6(clock_control_1_e_6), .f_6(clock_control_1_f_6),
    .g_5(clock_control_1_g_5), .Clock(clock_1_out), .Separator(clock_control_1_separator),
    .a(clock_control_1_a), .b(clock_control_1_b), .c(clock_control_1_c), .d(clock_control_1_d),
    .e(clock_control_1_e), .f(clock_control_1_f), .g(clock_control_1_g), .a_2(clock_control_1_a_2),
    .b_2(clock_control_1_b_2), .c_2(clock_control_1_c_2), .d_2(clock_control_1_d_2),
    .e_2(clock_control_1_e_2), .f_2(clock_control_1_f_2), .g_2(clock_control_1_g_2),
    .out_19(clock_control_1_out_19), .in_1(Second_up_out), .in_3(Minute_up_out), .in_4(Hour_up_out));
  _7_Segment_Display u_7_segment_display_1 (
    .g(clock_control_1_g_5), .f(clock_control_1_f_6), .a(clock_control_1_a_6), .b(clock_control_1_b_6),
    .e(clock_control_1_e_6), .d(clock_control_1_d_6), .c(clock_control_1_c_6));  // open: dp
  Clock_part #(.lowDuration(120)) clock_1 (.out(clock_1_out));
  Button Hour_up (.out(Hour_up_out));
  _7_Segment_Display u_7_segment_display_2 (
    .g(clock_control_1_g_4), .f(clock_control_1_f_4), .a(clock_control_1_a_4), .b(clock_control_1_b_4),
    .e(clock_control_1_e_4), .d(clock_control_1_d_4), .c(clock_control_1_c_4));  // open: dp
  _7_Segment_Display u_7_segment_display_3 (
    .g(clock_control_1_g_6), .f(clock_control_1_f_5), .a(clock_control_1_a_5), .b(clock_control_1_b_5),
    .e(clock_control_1_e_5), .d(clock_control_1_d_5), .c(clock_control_1_c_5), .dp(clock_control_1_separator));
  Button Minute_up (.out(Minute_up_out));
  _7_Segment_Display u_7_segment_display_4 (
    .g(clock_control_1_g_2), .f(clock_control_1_f_2), .a(clock_control_1_a_2), .b(clock_control_1_b_2),
    .e(clock_control_1_e_2), .d(clock_control_1_d_2), .c(clock_control_1_c_2));  // open: dp
  _7_Segment_Display u_7_segment_display_5 (
    .g(clock_control_1_g_3), .f(clock_control_1_f_3), .a(clock_control_1_a_3), .b(clock_control_1_b_3),
    .e(clock_control_1_e_3), .d(clock_control_1_d_3), .c(clock_control_1_c_3), .dp(clock_control_1_out_19));
  Button Second_up (.out(Second_up_out));
  _7_Segment_Display u_7_segment_display_6 (
    .g(clock_control_1_g), .f(clock_control_1_f), .a(clock_control_1_a), .b(clock_control_1_b),
    .e(clock_control_1_e), .d(clock_control_1_d), .c(clock_control_1_c));  // open: dp
endmodule
